# Fritzing sketch fritz_one_button_with_LEDs 2 (saved by Fritzing 0.9.4)
breadboards: 1

parts:
  Teensy_3_1 = Teensy 3.1
  R1 = Resistor [tolerance=±5% resistance=220 package="0805 [SMD]"]
  LED1 = smd LED [color="Red (633nm)" package="1206 [SMD]"]
  LED2 = LED - 3mm [color="Blue (525nm)" package="3 mm [THT]"]
  LED3 = LED - 3mm [color="Green (565nm)" package="3 mm [THT]"]
  R2 = Resistor [tolerance=±5% resistance=220 package="0805 [SMD]"]
  S1 = Pushbutton [package="[SMD]"]
  R3 = Trimmer Potentiometer [maximum_resistance=10kΩ package=THT]  # not connected
  R4 = Resistor [tolerance=±5% resistance=220 package="0805 [SMD]"]
  R5 = Resistor [tolerance=±5% resistance=220 package="0805 [SMD]"]

nets:
  N1: Teensy_3_1.D5, R4.Pin_0
  N2: Teensy_3_1.D6, R5.Pin_1
  N3: Teensy_3_1.D7, LED1.cathode, R2.Pin_0
  N4: Teensy_3_1.A7/D21, R1.Pin_1, S1.Pin_3, S1.Pin_4
  N5: R1.Pin_0, LED2.cathode, LED3.cathode, R2.Pin_1
  N6: LED2.anode, R5.Pin_0
  N7: LED3.anode, R4.Pin_1
  N8: S1.Pin_1, S1.Pin_2
